# Fritzing sketch ArduinoLidarLiteV3Diagram (saved by Fritzing 0.9.3b)
breadboards: 1

parts:
  Part1 = Arduino Due (Rev2b)
  HC-SR04_Sensor_1 = HC-SR04 Ultrasonic Distance Sensor
  J1 = Basic Servo
  VCC1 = 4 x AAA Battery Mount
  J2 = Basic Servo
  C1 = Electrolytic Capacitor [capacitance=4.7mF package="0605 [SMD, electrolytic]"]
  C3 = Electrolytic Capacitor [capacitance=1mF package="0605 [SMD, electrolytic]"]
  C4 = Electrolytic Capacitor [capacitance=1mF package="0605 [SMD, electrolytic]"]
  R1 = Resistor [tolerance=±5% resistance=4.7k package="2512 [SMD]"]
  R2 = Resistor [tolerance=±5% resistance=4.7k package="2512 [SMD]"]

nets:
  N1: Part1.D20/SDA3, HC-SR04_Sensor_1.TRIG, R2.Pin_1
  N2: Part1.D21/SCL3, HC-SR04_Sensor_1.ECHO, R1.Pin_1
  5V: Part1.5V, HC-SR04_Sensor_1.VCC, C1.+, C3.+, C4.+, R1.Pin_0, R2.Pin_0
  GND: Part1.GND, HC-SR04_Sensor_1.GND, J1.gnd, VCC1.-, J2.gnd, C1.-, C3.-, C4.-
  N3: Part1.D9_PWM, J2.pulse
  N4: Part1.D10_PWM/SS0, J1.pulse
  VCC: J1.vcc, VCC1.+, J2.vcc
