# Fritzing sketch ArduinoLidarLiteV3PerfboardDiagram (saved by Fritzing 0.9.3b)
perfboards: 1

parts:
  Part2 = Arduino Due (Rev2b)
  J3 = Camdenboss CTB0158-2 [part_number=CTB0158-2 package=THT]
  J4 = Camdenboss CTB0158-2 [part_number=CTB0158-2 package=THT]
  C5 = Electrolytic Capacitor [capacitance=4.7mF package="0605 [SMD, electrolytic]"]  # not connected
  C6 = Electrolytic Capacitor [capacitance=1mF package="0605 [SMD, electrolytic]"]  # not connected
  C7 = Electrolytic Capacitor [capacitance=4.7mF package="0605 [SMD, electrolytic]"]  # not connected
  R3 = Resistor [tolerance=±5% resistance=4.7k package="2512 [SMD]"]  # not connected
  R4 = Resistor [tolerance=±5% resistance=4.7k package="2512 [SMD]"]  # not connected
  J5 = Basic Servo
  J6 = Basic Servo  # not connected
  J7 = Camdenboss CTB0158-2 [part_number=CTB0158-2 package=THT]
  VCC2 = 4 x AAA Battery Mount
  Part3 = LIDAR-Lite

nets:
  N1: Part2.5V, J3.pin2
  N2: J3.terminal_1, Part3.GND
  N3: J3.terminal_2, Part3.5V
  N4: J4.terminal_1, Part3.SDA
  N5: J4.terminal_2, Part3.SCL
  N6: J5.gnd, J7.pin2
  N7: J5.vcc, J7.pin1
  N8: J7.terminal_1, VCC2.+
  N9: J7.terminal_2, VCC2.-

custom parts:
  LIDAR-Lite: PulsedLight LIDAR-Lite Sensor
