# Fritzing sketch ArduinoLidarTFMiniDiagram (saved by Fritzing 0.9.3b)
breadboards: 1

parts:
  Part1 = Arduino Due (Rev2b)
  HC-SR04_Sensor_1 = HC-SR04 Ultrasonic Distance Sensor
  J1 = Basic Servo
  VCC1 = 4 x AAA Battery Mount
  J2 = Basic Servo

nets:
  N1: Part1.D14/TX3, HC-SR04_Sensor_1.ECHO
  N2: Part1.D15/RX3, HC-SR04_Sensor_1.TRIG
  5V: Part1.5V, HC-SR04_Sensor_1.VCC
  GND: Part1.GND, HC-SR04_Sensor_1.GND, J1.gnd, VCC1.-, J2.gnd
  N3: Part1.D9_PWM, J2.pulse
  N4: Part1.D10_PWM/SS0, J1.pulse
  VCC: J1.vcc, VCC1.+, J2.vcc
